// Digital circuit lab2_part2.dig as structural Verilog
module lab2_part2 (
  input  in0,
  input  in1,
  input  in2,
  input  in3,
  output seg_a,
  output seg_f,
  output seg_b,
  output seg_g,
  output seg_e,
  output seg_c,
  output seg_d,
  output seg_dp,
  output sign_a,
  output sign_f,
  output sign_b,
  output sign_g,
  output sign_e,
  output sign_c,
  output sign_d,
  output sign_dp
);

  wire and_1_out, and_2_out, and_3_out, and_4_out, and_5_out, and_6_out, and_7_out, and_8_out, not_1_out,
       not_2_out, not_3_out, not_4_out, xor_1_out, xor_3_out, xor_4_out, xor_6_out, xor_7_out, xor_9_out,
       xor_10_out;
  wire [2:0] xor_2_out;

  Seven_Seg seven_seg_1 (.a(1'b0), .b(1'b0), .c(1'b0), .d(1'b0), .e(1'b0), .f(1'b0), .g(sign_g), .dp(1'b0));
  Seven_Seg seven_seg_2 (.a(seg_a), .b(seg_b), .c(seg_c), .d(seg_d), .e(seg_e), .f(seg_f), .g(seg_g), .dp(seg_dp));
  not not_1 (not_1_out, in0);
  xor xor_1 (xor_1_out, not_1_out, 1'b1);
  xor xor_2 (xor_2_out[0], 1'b0, xor_1_out);
  and and_1 (and_1_out, 1'b1, not_1_out);
  and and_2 (and_2_out, xor_1_out, 1'b0);
  xor xor_3 (xor_3_out, and_1_out, and_2_out);
  not not_2 (not_2_out, in1);
  xor xor_4 (xor_4_out, not_2_out, 1'b0);
  and and_3 (and_3_out, 1'b0, not_2_out);
  and and_4 (and_4_out, xor_4_out, xor_3_out);
  xor xor_5 (xor_2_out[1], xor_3_out, xor_4_out);
  Driver driver_1 (.out(seg_a));  // open: in, en
  Driver driver_2 (.out(seg_b));  // open: in, en
  Driver driver_3 (.out(seg_c));  // open: in, en
  Driver driver_4 (.out(seg_d));  // open: in, en
  Driver driver_5 (.out(seg_e));  // open: in, en
  Driver driver_6 (.out(seg_f));  // open: in, en
  Driver driver_7 (.out(seg_dp));  // open: in, en
  xor xor_6 (xor_6_out, and_3_out, and_4_out);
  Driver driver_8 (.out(seg_b));  // open: in, en
  Driver driver_9 (.out(seg_c));  // open: in, en
  Driver driver_10 (.out(seg_dp));  // open: in, en
  Driver driver_11 (.out(seg_a));  // open: in, en
  Driver driver_12 (.out(seg_b));  // open: in, en
  Driver driver_13 (.out(seg_d));  // open: in, en
  Driver driver_14 (.out(seg_e));  // open: in, en
  Driver driver_15 (.out(seg_g));  // open: in, en
  Driver driver_16 (.out(seg_dp));  // open: in, en
  Driver driver_17 (.out(seg_a));  // open: in, en
  Driver driver_18 (.out(seg_b));  // open: in, en
  Driver driver_19 (.out(seg_c));  // open: in, en
  Driver driver_20 (.out(seg_d));  // open: in, en
  Driver driver_21 (.out(seg_g));  // open: in, en
  Driver driver_22 (.out(seg_dp));  // open: in, en
  Driver driver_23 (.out(seg_a));  // open: in, en
  Driver driver_24 (.out(seg_b));  // open: in, en
  Driver driver_25 (.out(seg_c));  // open: in, en
  Driver driver_26 (.out(seg_g));  // open: in, en
  Driver driver_27 (.out(seg_dp));  // open: in, en
  Decoder #(.Selector_Bits(3)) decoder_1 (.sel(xor_2_out));  // open: out_0, out_1, out_2, out_3, out_4, out_5, out_6, out_7
  Driver driver_28 (.out(seg_a));  // open: in, en
  Driver driver_29 (.out(seg_b));  // open: in, en
  Driver driver_30 (.out(seg_c));  // open: in, en
  Driver driver_31 (.out(seg_dp));  // open: in, en
  Driver driver_32 (.out(seg_a));  // open: in, en
  Driver driver_33 (.out(seg_c));  // open: in, en
  Driver driver_34 (.out(seg_d));  // open: in, en
  Driver driver_35 (.out(seg_f));  // open: in, en
  Driver driver_36 (.out(seg_g));  // open: in, en
  Driver driver_37 (.out(seg_dp));  // open: in, en
  Driver driver_38 (.out(seg_a));  // open: in, en
  Driver driver_39 (.out(seg_c));  // open: in, en
  Driver driver_40 (.out(seg_d));  // open: in, en
  Driver driver_41 (.out(seg_f));  // open: in, en
  Driver driver_42 (.out(seg_g));  // open: in, en
  Driver driver_43 (.out(seg_dp));  // open: in, en
  not not_3 (not_3_out, in2);
  xor xor_7 (xor_7_out, not_3_out, 1'b0);
  xor xor_8 (xor_2_out[2], xor_6_out, xor_7_out);
  and and_5 (and_5_out, 1'b0, not_3_out);
  and and_6 (and_6_out, xor_7_out, xor_6_out);
  xor xor_9 (xor_9_out, and_5_out, and_6_out);
  not not_4 (not_4_out, in3);
  xor xor_10 (xor_10_out, not_4_out, 1'b0);
  and and_7 (and_7_out, 1'b0, not_4_out);
  and and_8 (and_8_out, xor_10_out, xor_9_out);
  xor xor_11 (sign_g, xor_9_out, xor_10_out);
  // XOr xor_12 has open pins: In_1=and_7_out, In_2=and_8_out, out=open

  assign sign_a = 1'b0;
  assign sign_b = 1'b0;
  assign sign_c = 1'b0;
  assign sign_d = 1'b0;
  assign sign_dp = 1'b0;
  assign sign_e = 1'b0;
  assign sign_f = 1'b0;

  // Notes on the sheet:
  //   Interface (do not edit the content inside this box)
  //   Outputs:
  //   Inputs
  //   Sign
  //   Decimal Number
endmodule

/* Test case:
in3 in2 in1 in0  sign_a sign_b sign_c sign_d sign_e sign_f sign_g  seg_a seg_b seg_c seg_d seg_e seg_f seg_g
 0   0   0   0    0      0      0      0      0      0      0       1     1     1     1     1     1     0
*/
